// Digital circuit cpu.dig as structural Verilog
module cpu (
  input  CLK
);

  wire branch_1_bt, control_unit_1_exec, forwarding_1_alu1, forwarding_1_alu2, multiplexer_2_out, not_1_out,
       or_1_out, or_2_out, reg_file_1_zero;
  wire [1:0] _1_s, ID_EX_PPR_q, ID_EX_PPR_q_5, multiplexer_3_out, register_1_q;
  wire [2:0] EX_WB_PPR_q, ID_EX_PPR_q_2, ID_EX_PPR_q_3;
  wire [3:0] alu_1_flag;
  wire [3:3] EX_WB_PPR_q_2;
  wire [7:0] ID_EX_PPR_q_8;
  wire [15:0] alu_1_result, and_1_out, EX_WB_PPR_q_3, ID_EX_PPR_q_6, ID_EX_PPR_q_7, multiplexer_1_out,
       multiplexer_4_out, multiplexer_5_out, multiplexer_6_out, notconnected_1_out, or_3_out,
       ramdualaccess_1_d1, ramdualaccess_1_d2, reg_file_1_pc;
  wire [15:8] IF_ID_PPR_q;
  wire [17:11] ID_EX_PPR_q_4;
  wire [19:0] multiplexer_7_out;
  wire [57:0] reg_file_1_out1;

  not not_1 (not_1_out, CLK);
  Multiplexer #(.Bits(16)) multiplexer_1 (
    .sel(or_1_out), .in_0(ramdualaccess_1_d2), .in_1({16{1'b0}}), .out(multiplexer_1_out));
  Register #(.Bits(16)) IF_ID_PPR (
    .D(multiplexer_1_out), .C(not_1_out), .en(1'b1),
    .Q({IF_ID_PPR_q[15:13], reg_file_1_out1[17], IF_ID_PPR_q[11:8], reg_file_1_out1[57:50]}));
  Multiplexer multiplexer_2 (
    .sel(ID_EX_PPR_q_4[16]), .in_0(reg_file_1_zero), .in_1(alu_1_flag[0]), .out(multiplexer_2_out));
  control_unit control_unit_1 (
    .INST({IF_ID_PPR_q[15:13], reg_file_1_out1[17], IF_ID_PPR_q[11:8], reg_file_1_out1[57:50]}),
    .ZERO(multiplexer_2_out), .ALUOP(reg_file_1_out1[1:0]), .RS1(reg_file_1_out1[4:2]),
    .RS2(reg_file_1_out1[7:5]), .WS(reg_file_1_out1[10:8]), .STR(reg_file_1_out1[11]),
    .WE(reg_file_1_out1[12]), .DMUX(reg_file_1_out1[14:13]), .LDR(reg_file_1_out1[15]),
    .FLEN(reg_file_1_out1[16]), .EXEC(control_unit_1_exec));
  LED led_1 (.in(control_unit_1_exec));
  reg_file reg_file_1 (
    .RS1(reg_file_1_out1[4:2]), .RS2(reg_file_1_out1[7:5]), .WS(EX_WB_PPR_q), .WE(EX_WB_PPR_q_2[3]),
    .IN(EX_WB_PPR_q_3), .clk(CLK), .FLEN(ID_EX_PPR_q_4[16]), .FLAG(alu_1_flag),
    .OUT1(reg_file_1_out1[33:18]), .OUT2(reg_file_1_out1[49:34]), .PC(reg_file_1_pc), .ZERO(reg_file_1_zero));
  or or_1 (or_1_out, register_1_q[0], register_1_q[1]);
  branch branch_1 (.WS(reg_file_1_out1[10:8]), .WE(reg_file_1_out1[12]), .BT(branch_1_bt));
  Multiplexer #(.Bits(2)) multiplexer_3 (.sel(branch_1_bt), .in_0(_1_s), .in_1(2'b10), .out(multiplexer_3_out));
  or or_2 (or_2_out, or_1_out, branch_1_bt);
  Register #(.Bits(2)) register_1 (.D(multiplexer_3_out), .C(CLK), .en(or_2_out), .Q(register_1_q));
  Sub #(.Bits(2)) _1 (.a(register_1_q), .b(2'b01), .c_i(1'b0), .s(_1_s));  // open: c_o
  Register #(.Bits(58)) ID_EX_PPR (
    .D(reg_file_1_out1), .C(not_1_out), .en(1'b1),
    .Q({ID_EX_PPR_q_8, ID_EX_PPR_q_7, ID_EX_PPR_q_6, ID_EX_PPR_q_4[17:15], ID_EX_PPR_q_5, multiplexer_7_out[3], ID_EX_PPR_q_4[11], multiplexer_7_out[2:0], ID_EX_PPR_q_3, ID_EX_PPR_q_2, ID_EX_PPR_q}));
  forwarding forwarding_1 (
    .ID_EX_RS1(ID_EX_PPR_q_2), .ID_EX_RS2(ID_EX_PPR_q_3), .EX_WB_WS(EX_WB_PPR_q),
    .EX_WB_WE(EX_WB_PPR_q_2[3]), .ALU1(forwarding_1_alu1), .ALU2(forwarding_1_alu2));
  Multiplexer #(.Bits(16)) multiplexer_4 (
    .sel(forwarding_1_alu2), .in_0(ID_EX_PPR_q_7), .in_1(EX_WB_PPR_q_3), .out(multiplexer_4_out));
  Multiplexer #(.Bits(16)) multiplexer_5 (
    .sel(forwarding_1_alu1), .in_0(ID_EX_PPR_q_6), .in_1(EX_WB_PPR_q_3), .out(multiplexer_5_out));
  assign and_1_out = 16'hff & multiplexer_4_out;  // And and_1, 16 bits wide
  alu alu_1 (
    .A(multiplexer_5_out), .B(multiplexer_4_out), .ALUOP(ID_EX_PPR_q), .RESULT(alu_1_result),
    .FLAG(alu_1_flag));
  assign or_3_out = {ID_EX_PPR_q_8, {8{1'b0}}} | and_1_out;  // Or or_3, 16 bits wide
  RAMDualAccess #(.AddrBits(16), .Bits(16)) ramdualaccess_1 (
    .str(ID_EX_PPR_q_4[11]), .C(CLK), .ld(ID_EX_PPR_q_4[15]), .A1(multiplexer_5_out),
    .Din1(multiplexer_4_out), .A2(reg_file_1_pc), .D1(ramdualaccess_1_d1), .D2(ramdualaccess_1_d2));
  Multiplexer #(.Bits(16)) multiplexer_6 (
    .sel(ID_EX_PPR_q_4[17]), .in_0({{8{1'b0}}, ID_EX_PPR_q_8}), .in_1(or_3_out), .out(multiplexer_6_out));
  Multiplexer #(.Selector_Bits(2), .Bits(16)) multiplexer_7 (
    .sel(ID_EX_PPR_q_5), .in_0(alu_1_result), .in_1(ramdualaccess_1_d1), .in_2(multiplexer_6_out),
    .in_3(notconnected_1_out), .out(multiplexer_7_out[19:4]));
  // NotConnected on notconnected_1_out
  // Probe IN on multiplexer_7_out[19:4]
  Register #(.Bits(20)) EX_WB_PPR (
    .D(multiplexer_7_out), .C(not_1_out), .en(1'b1), .Q({EX_WB_PPR_q_3, EX_WB_PPR_q_2[3], EX_WB_PPR_q}));
endmodule
